// Logisim project 8-bit reg.circ as structural Verilog: 2 circuits, main circuit main
module main (
  input  [1:0] in_1,
  input  in_2,
  input  [7:0] in_3,
  output [7:0] out_4
);

  wire clock_1_out;

  Clock clock_1 (.out(clock_1_out));
  _8_bit_register u_8_bit_register_1 (.CLK(clock_1_out), .FunSel(in_1), .E(in_2), .I(in_3), .Q(out_4));
endmodule

module _8_bit_register (
  input  CLK,
  input  [1:0] FunSel,
  input  E,
  input  [7:0] I,
  output [7:0] Q
);

  wire adder_1_cout, adder_1_out, adder_2_cout, adder_2_out, adder_3_cout, adder_3_out, adder_4_cout,
       adder_4_out, adder_5_cout, adder_5_out, adder_6_cout, adder_6_out, adder_7_cout, adder_7_out,
       adder_8_out, decoder_1_out0, decoder_1_out1, decoder_1_out2, decoder_1_out3, multiplexer_1_out,
       multiplexer_2_out, multiplexer_3_out, multiplexer_4_out, multiplexer_5_out, multiplexer_6_out,
       multiplexer_7_out, multiplexer_8_out;

  Decoder #(.select(2)) decoder_1 (
    .out0(decoder_1_out0), .out1(decoder_1_out1), .out2(decoder_1_out2), .out3(decoder_1_out3), .sel(FunSel),
    .en(E));
  Adder #(.width(1)) adder_1 (
    .a(Q[0]), .b(decoder_1_out3), .out(adder_1_out), .cin(decoder_1_out2), .cout(adder_1_cout));
  Adder #(.width(1)) adder_2 (.a(Q[1]), .b(decoder_1_out3), .out(adder_2_out), .cin(adder_1_cout), .cout(adder_2_cout));
  Adder #(.width(1)) adder_3 (.a(Q[2]), .b(decoder_1_out3), .out(adder_3_out), .cin(adder_2_cout), .cout(adder_3_cout));
  Adder #(.width(1)) adder_4 (.a(Q[3]), .b(decoder_1_out3), .out(adder_4_out), .cin(adder_3_cout), .cout(adder_4_cout));
  Adder #(.width(1)) adder_5 (.a(Q[4]), .b(decoder_1_out3), .out(adder_5_out), .cin(adder_4_cout), .cout(adder_5_cout));
  Adder #(.width(1)) adder_6 (.a(Q[5]), .b(decoder_1_out3), .out(adder_6_out), .cin(adder_5_cout), .cout(adder_6_cout));
  Adder #(.width(1)) adder_7 (.a(Q[6]), .b(decoder_1_out3), .out(adder_7_out), .cin(adder_6_cout), .cout(adder_7_cout));
  Adder #(.width(1)) adder_8 (.a(Q[7]), .b(decoder_1_out3), .out(adder_8_out), .cin(adder_7_cout));  // open: cout
  Multiplexer multiplexer_1 (.in0(adder_1_out), .in1(I[0]), .out(multiplexer_1_out), .sel(decoder_1_out1), .en(E));
  Multiplexer multiplexer_2 (.in0(adder_2_out), .in1(I[1]), .out(multiplexer_2_out), .sel(decoder_1_out1), .en(E));
  Multiplexer multiplexer_3 (.in0(adder_3_out), .in1(I[2]), .out(multiplexer_3_out), .sel(decoder_1_out1), .en(E));
  Multiplexer multiplexer_4 (.in0(adder_4_out), .in1(I[3]), .out(multiplexer_4_out), .sel(decoder_1_out1), .en(E));
  Multiplexer multiplexer_5 (.in0(adder_5_out), .in1(I[4]), .out(multiplexer_5_out), .sel(decoder_1_out1), .en(E));
  Multiplexer multiplexer_6 (.in0(adder_6_out), .in1(I[5]), .out(multiplexer_6_out), .sel(decoder_1_out1), .en(E));
  Multiplexer multiplexer_7 (.in0(adder_7_out), .in1(I[6]), .out(multiplexer_7_out), .sel(decoder_1_out1), .en(E));
  Multiplexer multiplexer_8 (.in0(adder_8_out), .in1(I[7]), .out(multiplexer_8_out), .sel(decoder_1_out1), .en(E));
  D_Flip_Flop d_ff_1 (.clk(CLK), .D(multiplexer_1_out), .Q(Q[0]), .en(E), .reset(decoder_1_out0));  // open: Qn, preset
  D_Flip_Flop d_ff_2 (.clk(CLK), .D(multiplexer_2_out), .Q(Q[1]), .en(E), .reset(decoder_1_out0));  // open: Qn, preset
  D_Flip_Flop d_ff_3 (.clk(CLK), .D(multiplexer_3_out), .Q(Q[2]), .en(E), .reset(decoder_1_out0));  // open: Qn, preset
  D_Flip_Flop d_ff_4 (.clk(CLK), .D(multiplexer_4_out), .Q(Q[3]), .en(E), .reset(decoder_1_out0));  // open: Qn, preset
  D_Flip_Flop d_ff_5 (.clk(CLK), .D(multiplexer_5_out), .Q(Q[4]), .en(E), .reset(decoder_1_out0));  // open: Qn, preset
  D_Flip_Flop d_ff_6 (.clk(CLK), .D(multiplexer_6_out), .Q(Q[5]), .en(E), .reset(decoder_1_out0));  // open: Qn, preset
  D_Flip_Flop d_ff_7 (.clk(CLK), .D(multiplexer_7_out), .Q(Q[6]), .en(E), .reset(decoder_1_out0));  // open: Qn, preset
  D_Flip_Flop d_ff_8 (.clk(CLK), .D(multiplexer_8_out), .Q(Q[7]), .en(E), .reset(decoder_1_out0));  // open: Qn, preset
endmodule
