// Logisim project registers.circ as structural Verilog: 3 circuits, main circuit main
module main (
  input  [1:0] FunSel,
  input  [1:0] FunSel_2,
  input  E,
  input  E_2,
  input  [7:0] I,
  input  [15:0] I_2,
  output [7:0] O,
  output [15:0] O_2
);

  wire clock_1_out;

  Clock clock_1 (.out(clock_1_out));
  _16_bit_register u_16_bit_register_1 (.CLK(clock_1_out), .FunSel(FunSel_2), .E(E_2), .I(I_2), .out_5(O_2));
  _8_bit_register u_8_bit_register_1 (.CLK(clock_1_out), .FunSel(FunSel), .E(E), .I(I), .Q(O));
endmodule

module _8_bit_register (
  input  CLK,
  input  [1:0] FunSel,
  input  E,
  input  [7:0] I,
  output [7:0] Q
);

  wire adder_1_cout, adder_1_out, adder_2_cout, adder_2_out, adder_3_cout, adder_3_out, adder_4_cout,
       adder_4_out, adder_5_cout, adder_5_out, adder_6_cout, adder_6_out, adder_7_cout, adder_7_out,
       adder_8_out, decoder_1_out0, decoder_1_out1, decoder_1_out2, decoder_1_out3, multiplexer_1_out,
       multiplexer_2_out, multiplexer_3_out, multiplexer_4_out, multiplexer_5_out, multiplexer_6_out,
       multiplexer_7_out, multiplexer_8_out;

  Decoder #(.select(2)) decoder_1 (
    .out0(decoder_1_out0), .out1(decoder_1_out1), .out2(decoder_1_out2), .out3(decoder_1_out3), .sel(FunSel),
    .en(E));
  Adder #(.width(1)) adder_1 (
    .a(Q[0]), .b(decoder_1_out3), .out(adder_1_out), .cin(decoder_1_out2), .cout(adder_1_cout));
  Adder #(.width(1)) adder_2 (.a(Q[1]), .b(decoder_1_out3), .out(adder_2_out), .cin(adder_1_cout), .cout(adder_2_cout));
  Adder #(.width(1)) adder_3 (.a(Q[2]), .b(decoder_1_out3), .out(adder_3_out), .cin(adder_2_cout), .cout(adder_3_cout));
  Adder #(.width(1)) adder_4 (.a(Q[3]), .b(decoder_1_out3), .out(adder_4_out), .cin(adder_3_cout), .cout(adder_4_cout));
  Adder #(.width(1)) adder_5 (.a(Q[4]), .b(decoder_1_out3), .out(adder_5_out), .cin(adder_4_cout), .cout(adder_5_cout));
  Adder #(.width(1)) adder_6 (.a(Q[5]), .b(decoder_1_out3), .out(adder_6_out), .cin(adder_5_cout), .cout(adder_6_cout));
  Adder #(.width(1)) adder_7 (.a(Q[6]), .b(decoder_1_out3), .out(adder_7_out), .cin(adder_6_cout), .cout(adder_7_cout));
  Adder #(.width(1)) adder_8 (.a(Q[7]), .b(decoder_1_out3), .out(adder_8_out), .cin(adder_7_cout));  // open: cout
  Multiplexer multiplexer_1 (.in0(adder_1_out), .in1(I[0]), .out(multiplexer_1_out), .sel(decoder_1_out1), .en(E));
  Multiplexer multiplexer_2 (.in0(adder_2_out), .in1(I[1]), .out(multiplexer_2_out), .sel(decoder_1_out1), .en(E));
  Multiplexer multiplexer_3 (.in0(adder_3_out), .in1(I[2]), .out(multiplexer_3_out), .sel(decoder_1_out1), .en(E));
  Multiplexer multiplexer_4 (.in0(adder_4_out), .in1(I[3]), .out(multiplexer_4_out), .sel(decoder_1_out1), .en(E));
  Multiplexer multiplexer_5 (.in0(adder_5_out), .in1(I[4]), .out(multiplexer_5_out), .sel(decoder_1_out1), .en(E));
  Multiplexer multiplexer_6 (.in0(adder_6_out), .in1(I[5]), .out(multiplexer_6_out), .sel(decoder_1_out1), .en(E));
  Multiplexer multiplexer_7 (.in0(adder_7_out), .in1(I[6]), .out(multiplexer_7_out), .sel(decoder_1_out1), .en(E));
  Multiplexer multiplexer_8 (.in0(adder_8_out), .in1(I[7]), .out(multiplexer_8_out), .sel(decoder_1_out1), .en(E));
  D_Flip_Flop d_ff_1 (.clk(CLK), .D(multiplexer_1_out), .Q(Q[0]), .en(E), .reset(decoder_1_out0));  // open: Qn, preset
  D_Flip_Flop d_ff_2 (.clk(CLK), .D(multiplexer_2_out), .Q(Q[1]), .en(E), .reset(decoder_1_out0));  // open: Qn, preset
  D_Flip_Flop d_ff_3 (.clk(CLK), .D(multiplexer_3_out), .Q(Q[2]), .en(E), .reset(decoder_1_out0));  // open: Qn, preset
  D_Flip_Flop d_ff_4 (.clk(CLK), .D(multiplexer_4_out), .Q(Q[3]), .en(E), .reset(decoder_1_out0));  // open: Qn, preset
  D_Flip_Flop d_ff_5 (.clk(CLK), .D(multiplexer_5_out), .Q(Q[4]), .en(E), .reset(decoder_1_out0));  // open: Qn, preset
  D_Flip_Flop d_ff_6 (.clk(CLK), .D(multiplexer_6_out), .Q(Q[5]), .en(E), .reset(decoder_1_out0));  // open: Qn, preset
  D_Flip_Flop d_ff_7 (.clk(CLK), .D(multiplexer_7_out), .Q(Q[6]), .en(E), .reset(decoder_1_out0));  // open: Qn, preset
  D_Flip_Flop d_ff_8 (.clk(CLK), .D(multiplexer_8_out), .Q(Q[7]), .en(E), .reset(decoder_1_out0));  // open: Qn, preset
endmodule

module _16_bit_register (
  input  CLK,
  input  [1:0] FunSel,
  input  E,
  input  [15:0] I,
  output [15:0] out_5
);

  wire adder_1_cout, adder_1_out, adder_2_cout, adder_2_out, adder_3_cout, adder_3_out, adder_4_cout,
       adder_4_out, adder_5_cout, adder_5_out, adder_6_cout, adder_6_out, adder_7_cout, adder_7_out,
       adder_8_cout, adder_8_out, adder_9_cout, adder_9_out, adder_10_cout, adder_10_out, adder_11_cout,
       adder_11_out, adder_12_cout, adder_12_out, adder_13_cout, adder_13_out, adder_14_cout, adder_14_out,
       adder_15_cout, adder_15_out, adder_16_out, decoder_1_out0, decoder_1_out1, decoder_1_out2,
       decoder_1_out3, multiplexer_1_out, multiplexer_2_out, multiplexer_3_out, multiplexer_4_out,
       multiplexer_5_out, multiplexer_6_out, multiplexer_7_out, multiplexer_8_out, multiplexer_9_out,
       multiplexer_10_out, multiplexer_11_out, multiplexer_12_out, multiplexer_13_out, multiplexer_14_out,
       multiplexer_15_out, multiplexer_16_out;

  Decoder #(.select(2)) decoder_1 (
    .out0(decoder_1_out0), .out1(decoder_1_out1), .out2(decoder_1_out2), .out3(decoder_1_out3), .sel(FunSel),
    .en(E));
  Adder #(.width(1)) adder_1 (
    .a(out_5[0]), .b(decoder_1_out3), .out(adder_1_out), .cin(decoder_1_out2), .cout(adder_1_cout));
  Adder #(.width(1)) adder_2 (
    .a(out_5[1]), .b(decoder_1_out3), .out(adder_2_out), .cin(adder_1_cout), .cout(adder_2_cout));
  Adder #(.width(1)) adder_3 (
    .a(out_5[2]), .b(decoder_1_out3), .out(adder_3_out), .cin(adder_2_cout), .cout(adder_3_cout));
  Adder #(.width(1)) adder_4 (
    .a(out_5[3]), .b(decoder_1_out3), .out(adder_4_out), .cin(adder_3_cout), .cout(adder_4_cout));
  Adder #(.width(1)) adder_5 (
    .a(out_5[4]), .b(decoder_1_out3), .out(adder_5_out), .cin(adder_4_cout), .cout(adder_5_cout));
  Adder #(.width(1)) adder_6 (
    .a(out_5[5]), .b(decoder_1_out3), .out(adder_6_out), .cin(adder_5_cout), .cout(adder_6_cout));
  Adder #(.width(1)) adder_7 (
    .a(out_5[6]), .b(decoder_1_out3), .out(adder_7_out), .cin(adder_6_cout), .cout(adder_7_cout));
  Adder #(.width(1)) adder_8 (
    .a(out_5[7]), .b(decoder_1_out3), .out(adder_8_out), .cin(adder_7_cout), .cout(adder_8_cout));
  Adder #(.width(1)) adder_9 (
    .a(out_5[8]), .b(decoder_1_out3), .out(adder_9_out), .cin(adder_8_cout), .cout(adder_9_cout));
  Adder #(.width(1)) adder_10 (
    .a(out_5[9]), .b(decoder_1_out3), .out(adder_10_out), .cin(adder_9_cout), .cout(adder_10_cout));
  Adder #(.width(1)) adder_11 (
    .a(out_5[10]), .b(decoder_1_out3), .out(adder_11_out), .cin(adder_10_cout), .cout(adder_11_cout));
  Adder #(.width(1)) adder_12 (
    .a(out_5[11]), .b(decoder_1_out3), .out(adder_12_out), .cin(adder_11_cout), .cout(adder_12_cout));
  Adder #(.width(1)) adder_13 (
    .a(out_5[12]), .b(decoder_1_out3), .out(adder_13_out), .cin(adder_12_cout), .cout(adder_13_cout));
  Adder #(.width(1)) adder_14 (
    .a(out_5[13]), .b(decoder_1_out3), .out(adder_14_out), .cin(adder_13_cout), .cout(adder_14_cout));
  Adder #(.width(1)) adder_15 (
    .a(out_5[14]), .b(decoder_1_out3), .out(adder_15_out), .cin(adder_14_cout), .cout(adder_15_cout));
  Adder #(.width(1)) adder_16 (
    .a(out_5[15]), .b(decoder_1_out3), .out(adder_16_out), .cin(adder_15_cout));  // open: cout
  Multiplexer multiplexer_1 (.in0(adder_1_out), .in1(I[0]), .out(multiplexer_1_out), .sel(decoder_1_out1), .en(E));
  Multiplexer multiplexer_2 (.in0(adder_2_out), .in1(I[1]), .out(multiplexer_2_out), .sel(decoder_1_out1), .en(E));
  Multiplexer multiplexer_3 (.in0(adder_3_out), .in1(I[2]), .out(multiplexer_3_out), .sel(decoder_1_out1), .en(E));
  Multiplexer multiplexer_4 (.in0(adder_4_out), .in1(I[3]), .out(multiplexer_4_out), .sel(decoder_1_out1), .en(E));
  Multiplexer multiplexer_5 (.in0(adder_5_out), .in1(I[4]), .out(multiplexer_5_out), .sel(decoder_1_out1), .en(E));
  Multiplexer multiplexer_6 (.in0(adder_6_out), .in1(I[5]), .out(multiplexer_6_out), .sel(decoder_1_out1), .en(E));
  Multiplexer multiplexer_7 (.in0(adder_7_out), .in1(I[6]), .out(multiplexer_7_out), .sel(decoder_1_out1), .en(E));
  Multiplexer multiplexer_8 (.in0(adder_8_out), .in1(I[7]), .out(multiplexer_8_out), .sel(decoder_1_out1), .en(E));
  Multiplexer multiplexer_9 (.in0(adder_9_out), .in1(I[8]), .out(multiplexer_9_out), .sel(decoder_1_out1), .en(E));
  Multiplexer multiplexer_10 (.in0(adder_10_out), .in1(I[9]), .out(multiplexer_10_out), .sel(decoder_1_out1), .en(E));
  Multiplexer multiplexer_11 (.in0(adder_11_out), .in1(I[10]), .out(multiplexer_11_out), .sel(decoder_1_out1), .en(E));
  Multiplexer multiplexer_12 (.in0(adder_12_out), .in1(I[11]), .out(multiplexer_12_out), .sel(decoder_1_out1), .en(E));
  Multiplexer multiplexer_13 (.in0(adder_13_out), .in1(I[12]), .out(multiplexer_13_out), .sel(decoder_1_out1), .en(E));
  Multiplexer multiplexer_14 (.in0(adder_14_out), .in1(I[13]), .out(multiplexer_14_out), .sel(decoder_1_out1), .en(E));
  Multiplexer multiplexer_15 (.in0(adder_15_out), .in1(I[14]), .out(multiplexer_15_out), .sel(decoder_1_out1), .en(E));
  Multiplexer multiplexer_16 (.in0(adder_16_out), .in1(I[15]), .out(multiplexer_16_out), .sel(decoder_1_out1), .en(E));
  D_Flip_Flop d_ff_1 (
    .clk(CLK), .D(multiplexer_1_out), .Q(out_5[0]), .en(E), .reset(decoder_1_out0));  // open: Qn, preset
  D_Flip_Flop d_ff_2 (
    .clk(CLK), .D(multiplexer_2_out), .Q(out_5[1]), .en(E), .reset(decoder_1_out0));  // open: Qn, preset
  D_Flip_Flop d_ff_3 (
    .clk(CLK), .D(multiplexer_3_out), .Q(out_5[2]), .en(E), .reset(decoder_1_out0));  // open: Qn, preset
  D_Flip_Flop d_ff_4 (
    .clk(CLK), .D(multiplexer_4_out), .Q(out_5[3]), .en(E), .reset(decoder_1_out0));  // open: Qn, preset
  D_Flip_Flop d_ff_5 (
    .clk(CLK), .D(multiplexer_5_out), .Q(out_5[4]), .en(E), .reset(decoder_1_out0));  // open: Qn, preset
  D_Flip_Flop d_ff_6 (
    .clk(CLK), .D(multiplexer_6_out), .Q(out_5[5]), .en(E), .reset(decoder_1_out0));  // open: Qn, preset
  D_Flip_Flop d_ff_7 (
    .clk(CLK), .D(multiplexer_7_out), .Q(out_5[6]), .en(E), .reset(decoder_1_out0));  // open: Qn, preset
  D_Flip_Flop d_ff_8 (
    .clk(CLK), .D(multiplexer_8_out), .Q(out_5[7]), .en(E), .reset(decoder_1_out0));  // open: Qn, preset
  D_Flip_Flop d_ff_9 (
    .clk(CLK), .D(multiplexer_9_out), .Q(out_5[8]), .en(E), .reset(decoder_1_out0));  // open: Qn, preset
  D_Flip_Flop d_ff_10 (
    .clk(CLK), .D(multiplexer_10_out), .Q(out_5[9]), .en(E), .reset(decoder_1_out0));  // open: Qn, preset
  D_Flip_Flop d_ff_11 (
    .clk(CLK), .D(multiplexer_11_out), .Q(out_5[10]), .en(E), .reset(decoder_1_out0));  // open: Qn, preset
  D_Flip_Flop d_ff_12 (
    .clk(CLK), .D(multiplexer_12_out), .Q(out_5[11]), .en(E), .reset(decoder_1_out0));  // open: Qn, preset
  D_Flip_Flop d_ff_13 (
    .clk(CLK), .D(multiplexer_13_out), .Q(out_5[12]), .en(E), .reset(decoder_1_out0));  // open: Qn, preset
  D_Flip_Flop d_ff_14 (
    .clk(CLK), .D(multiplexer_14_out), .Q(out_5[13]), .en(E), .reset(decoder_1_out0));  // open: Qn, preset
  D_Flip_Flop d_ff_15 (
    .clk(CLK), .D(multiplexer_15_out), .Q(out_5[14]), .en(E), .reset(decoder_1_out0));  // open: Qn, preset
  D_Flip_Flop d_ff_16 (
    .clk(CLK), .D(multiplexer_16_out), .Q(out_5[15]), .en(E), .reset(decoder_1_out0));  // open: Qn, preset
endmodule
