// Logisim project part1.circ as structural Verilog: 1 circuit, main circuit main
module main (
);

  LED led_1 (.in(1'b1));
  LED led_2 (.in(1'b0));

  // Notes on the sheet:
  //   5V
  //   GND
  //   High
  //   Low
endmodule
