// Logisim project part2.circ as structural Verilog: 1 circuit, main circuit main
module main (
  input  Input
);

  wire n7404_1_p2;

  // _7404 7404_1: pin names not known; wires that end beside it: Input, n7404_1_p2, Input, 1'b1, 1'b0
  LED led_1 (.in(Input));
  LED led_2 (.in(n7404_1_p2));

  // Notes on the sheet:
  //   4Y
  //   4A
  //   Vcc
  //   5V
  //   GND
  //   GND
  //   Monitor
  //   Input
  //   Output
endmodule
