// Logisim project part1.circ as structural Verilog: 1 circuit, main circuit main
module main (
  input  a,
  input  b,
  output \F₁ ,
  output \F₂ 
);

  wire and_1_out, not_1_out, or_1_out, or_2_out;

  and and_1 (and_1_out, a, b);
  or or_1 (or_1_out, a, b);
  or or_2 (or_2_out, a, not_1_out);
  not not_1 (not_1_out, b);
  or or_3 (\F₁ , and_1_out, a);
  and and_2 (\F₂ , or_1_out, or_2_out);

  // Notes on the sheet:
  //   PART 1
endmodule
