// Logisim project part1_IC.circ as structural Verilog: 1 circuit, main circuit main
module main (
  input  a,
  input  b,
  output F1,
  output F2
);

  wire n7404_1_p4, n7408_1_p4, n7408_1_p6, n7408_1_p7;

  // _7404 7404_1: pin names not known; wires that end beside it: b, 1'b1, b, n7404_1_p4, a, b
  // _7408 7408_1: pin names not known; wires that end beside it: 1'b0, a, b, n7408_1_p4, 1'b1, n7408_1_p6, n7408_1_p7, F2
  // _7432 7432_1: pin names not known; wires that end beside it: 1'b0, n7408_1_p4, a, F1, 1'b0, 1'b1, n7404_1_p4, a, n7408_1_p7, a, b, n7408_1_p6, 1'b1

  // Notes on the sheet:
  //   GND
  //   5V
  //   PART 1
endmodule
