// Logisim project part1_IC.circ as structural Verilog: 1 circuit, main circuit main
module main (
  input  a,
  input  b,
  output out_3,
  output out_4
);

  wire n7404_1_p4, n7404_1_p5, n7408_1_p3, n7432_2_p3;

  // _7404 7404_1: pin names not known; wires that end beside it: a, b, b, n7404_1_p4, n7404_1_p5
  // _7408 7408_1: pin names not known; wires that end beside it: a, b, n7408_1_p3
  // _7432 7432_1: pin names not known; wires that end beside it: n7408_1_p3, a, out_3
  // _7432 7432_2: pin names not known; wires that end beside it: a, b, n7432_2_p3
  // _7432 7432_3: pin names not known; wires that end beside it: a, n7404_1_p4
  // _7408 7408_2: pin names not known; wires that end beside it: n7432_2_p3, n7404_1_p5, out_4

  // Notes on the sheet:
  //   PART 1
endmodule
