// Logisim project part2_IC.circ as structural Verilog: 1 circuit, main circuit main
module main (
  input  a,
  input  b,
  output a___a_b,
  output a__a_b
);

  wire n7408_1_p3, n7408_1_p6;

  // _7408 7408_1: pin names not known; wires that end beside it: a, b, n7408_1_p3, 1'b1, a, n7408_1_p6, a__a_b, a, b
  // _7432 7432_1: pin names not known; wires that end beside it: 1'b0, n7408_1_p3, a, a___a_b, 1'b0, 1'b1, b, a, n7408_1_p6

  // Notes on the sheet:
  //   GND
  //   5V
  //   PART 2
endmodule
