// Logisim project part3.circ as structural Verilog: 1 circuit, main circuit main
module main (
  input  a,
  input  b,
  input  c,
  output \F₃_prime 
);

  wire not_1_out, not_2_out, not_3_out, or_1_out, or_2_out;

  not not_1 (not_1_out, a);
  not not_2 (not_2_out, b);
  not not_3 (not_3_out, c);
  or or_1 (or_1_out, not_1_out, not_2_out);
  or or_2 (or_2_out, a, not_3_out);
  and and_1 (\F₃_prime , or_1_out, or_2_out);

  // Notes on the sheet:
  //   PART 3
endmodule
