// Logisim project part3_IC.circ as structural Verilog: 1 circuit, main circuit main
module main (
  input  a,
  input  b,
  input  c,
  output \F₃_prime 
);

  wire n7404_1_p2, n7404_1_p4, n7404_1_p7, n7432_1_p4, n7432_1_p8;

  // _7404 7404_1: pin names not known; wires that end beside it: a, n7404_1_p2, b, n7404_1_p4, 1'b1, c, n7404_1_p7, a, b, c
  // _7432 7432_1: pin names not known; wires that end beside it: 1'b0, n7404_1_p4, n7404_1_p2, n7432_1_p4, 1'b1, n7404_1_p7, a, n7432_1_p8
  // _7408 7408_1: pin names not known; wires that end beside it: 1'b0, n7432_1_p4, n7432_1_p8, \F₃_prime , 1'b0, 1'b1

  // Notes on the sheet:
  //   GND
  //   5V
  //   PART 3
endmodule
