// Logisim project part4_IC.circ as structural Verilog: 1 circuit, main circuit main
module main (
  input  c,
  input  d,
  output \F₄ 
);

  wire n7404_1_p2, n7404_1_p5, n7408_1_p4, n7408_1_p8;

  // _7404 7404_1: pin names not known; wires that end beside it: d, n7404_1_p2, 1'b1, c, n7404_1_p5, c, d
  // _7408 7408_1: pin names not known; wires that end beside it: 1'b0, n7404_1_p2, c, n7408_1_p4, 1'b1, n7404_1_p5, d, n7408_1_p8
  // _7432 7432_1: pin names not known; wires that end beside it: 1'b0, n7408_1_p4, n7408_1_p8, \F₄ , 1'b0, 1'b1

  // Notes on the sheet:
  //   GND
  //   5V
  //   PART 4
endmodule
