// Logisim project part4_IC.circ as structural Verilog: 1 circuit, main circuit main
module main (
  input  c,
  input  d,
  output out_3
);

  wire n7404_1_p2, n7404_2_p2, n7408_1_p3, n7408_2_p5;

  // _7404 7404_1: pin names not known; wires that end beside it: d, n7404_1_p2
  // _7404 7404_2: pin names not known; wires that end beside it: c, n7404_2_p2
  // _7408 7408_1: pin names not known; wires that end beside it: c, n7404_1_p2, n7408_1_p3
  // _7408 7408_2: pin names not known; wires that end beside it: c, d, n7404_2_p2, d, n7408_2_p5
  // _7432 7432_1: pin names not known; wires that end beside it: n7408_1_p3, n7408_2_p5, out_3

  // Notes on the sheet:
  //   PART 4
endmodule
