// Logisim project part1.circ as structural Verilog: 2 circuits, main circuit main
module main (
  input  a,
  input  b,
  input  c,
  input  d,
  output F
);

  wire dip_7404_1_p2, dip_7404_1_p4, dip_7404_1_p6, dip_7408_1_p4, dip_7408_1_p7, dip_7408_1_p8,
       dip_7411_1_p5, dip_7432_1_p4, dip_7432_1_p7;

  // DIP_7404 dip_7404_1: pin names not known; wires that end beside it: a, dip_7404_1_p2, b, dip_7404_1_p4, c, dip_7404_1_p6, 1'b1
  // DIP_7411 dip_7411_1: pin names not known; wires that end beside it: 1'b0, dip_7404_1_p6, dip_7404_1_p4, dip_7404_1_p2, dip_7411_1_p5, 1'b1, dip_7404_1_p6, b, a
  // DIP_7408 dip_7408_1: pin names not known; wires that end beside it: 1'b0, b, d, dip_7408_1_p4, c, d, dip_7408_1_p7, dip_7408_1_p8, 1'b1
  // DIP_7432 dip_7432_1: pin names not known; wires that end beside it: 1'b0, dip_7411_1_p5, dip_7408_1_p8, dip_7432_1_p4, dip_7408_1_p4, dip_7408_1_p7, dip_7432_1_p7, 1'b0, 1'b1, dip_7432_1_p4, dip_7432_1_p7, F

  // Notes on the sheet:
  //   GND
  //   5V
  //   PART 1
endmodule

module main2 (
  input  a,
  input  b,
  input  c,
  input  d,
  output F
);

  wire and_1_out, and_2_out, and_3_out, and_4_out, not_1_out, not_2_out, not_3_out, not_4_out, or_1_out,
       or_3_out;

  not not_1 (not_1_out, a);
  not not_2 (not_2_out, b);
  and and_1 (and_1_out, not_1_out, not_2_out, not_3_out);
  not not_3 (not_3_out, c);
  and and_2 (and_2_out, b, d);
  and and_3 (and_3_out, c, d);
  and and_4 (and_4_out, a, b, not_4_out);
  not not_4 (not_4_out, c);
  or or_1 (or_1_out, and_1_out, and_2_out);
  or or_2 (F, or_1_out, or_3_out);
  or or_3 (or_3_out, and_3_out, and_4_out);

  // Notes on the sheet:
  //   PART 1
endmodule
