// Logisim project part2.circ as structural Verilog: 2 circuits, main circuit main
module main (
  input  a,
  input  b,
  input  c,
  input  d,
  output F
);

  wire nand_1_out, nand_2_out, nand_3_out, nand_4_out, nand_5_out, nand_6_out, not_1_out, not_2_out,
       not_3_out, not_4_out, not_5_out, not_6_out, not_7_out;

  not not_1 (not_1_out, a);
  not not_2 (not_2_out, b);
  not not_3 (not_3_out, c);
  not not_4 (not_4_out, a);
  not not_5 (not_5_out, c);
  nand nand_1 (nand_1_out, not_1_out, not_2_out, not_3_out);
  nand nand_2 (nand_2_out, not_4_out, d);
  nand nand_3 (nand_3_out, c, d);
  nand nand_4 (nand_4_out, a, b, not_5_out);
  nand nand_5 (nand_5_out, nand_1_out, nand_2_out);
  not not_6 (not_6_out, nand_5_out);
  not not_7 (not_7_out, nand_6_out);
  nand nand_6 (nand_6_out, nand_3_out, nand_4_out);
  nand nand_7 (F, not_6_out, not_7_out);

  // Notes on the sheet:
  //   PART 2
endmodule

module main2 (
  input  a,
  input  b,
  input  c,
  input  d,
  output out_5
);

  wire n7400_1_p3, n7400_1_p10, n7404_1_p2, n7404_1_p4, n7404_1_p6, n7404_1_p9, n7404_1_p10, n7404_1_p11,
       n7404_1_p12, n7410_1_p6, n7410_1_p10;

  // _7404 7404_1: pin names not known; wires that end beside it: a, n7404_1_p2, b, n7404_1_p4, c, n7404_1_p6, 1'b0, 1'b1, n7404_1_p9, n7404_1_p10, n7404_1_p11, n7404_1_p12
  // _7410 7410_1: pin names not known; wires that end beside it: n7404_1_p6, n7404_1_p4, a, b, n7404_1_p6, n7410_1_p6, 1'b0, 1'b1, n7404_1_p2, n7410_1_p10, n7404_1_p12, n7404_1_p10, 1'b1, out_5
  // _7400 7400_1: pin names not known; wires that end beside it: n7404_1_p2, d, n7400_1_p3, n7400_1_p3, n7410_1_p10, n7404_1_p11, 1'b0, 1'b1, n7410_1_p6, n7400_1_p10, n7404_1_p9, c, d, n7400_1_p10

  // Notes on the sheet:
  //   GND
  //   5V
  //   PART 2
endmodule
