// Logisim project part3.circ as structural Verilog: 2 circuits, main circuit main
module main (
  input  d,
  input  a,
  input  b,
  input  c,
  output _4
);

  Multiplexer #(.select(3), .enable("false")) multiplexer_1 (
    .in0(1'b1), .in1(d), .in2(d), .in3(d), .in4(1'b0), .in5(d), .in6(1'b1), .in7(1'b0), .out(_4),
    .sel({a, b, c}));

  // Notes on the sheet:
  //   1
  //   2
  //   3
  //   5
  //   6
  //   7
  //   PART 3
endmodule

module main2 (
  input  a,
  input  b,
  input  c,
  input  d,
  input  E_prime,
  output out_6
);

  // _74151 74151_1: pin names not known; wires that end beside it: d, d, d, 1'b1, out_6, E_prime, 1'b0, 1'b1, 1'b0, d, 1'b1, 1'b0, c, b, a

  // Notes on the sheet:
  //   PART 3
endmodule
