// Logisim project part4_a.circ as structural Verilog: 2 circuits, main circuit main
module main (
  input  a,
  input  b,
  input  c,
  output F1
);

  wire decoder_1_out0, decoder_1_out2, decoder_1_out3, decoder_1_out7;

  Decoder #(.select(3), .enable("false")) decoder_1 (
    .out0(decoder_1_out0), .out2(decoder_1_out2), .out3(decoder_1_out3), .out7(decoder_1_out7),
    .sel({a, b, c}));  // open: out1, out4, out5, out6
  or or_1 (F1, decoder_1_out0, decoder_1_out2, decoder_1_out3, decoder_1_out7);

  // Notes on the sheet:
  //   PART 4.a
endmodule

module main2 (
  input  a,
  input  b,
  input  c,
  output out_4
);

  wire n7404_1_p3, n7404_1_p6, n7404_1_p8, n7432_1_p2, n7432_1_p4, n7432_1_p10, n74138_1_p7, n74138_1_p9,
       n74138_1_p10, n74138_1_p11;

  // _74138 74138_1: pin names not known; wires that end beside it: c, b, a, 1'b0, 1'b0, 1'b1, n74138_1_p7, 1'b1, n74138_1_p9, n74138_1_p10, n74138_1_p11
  // _7404 7404_1: pin names not known; wires that end beside it: 1'b0, n74138_1_p7, n7404_1_p3, 1'b1, n74138_1_p11, n7404_1_p6, n74138_1_p10, n7404_1_p8, n74138_1_p9
  // _7432 7432_1: pin names not known; wires that end beside it: 1'b0, n7432_1_p2, n7404_1_p3, n7432_1_p4, 1'b0, n7432_1_p2, 1'b1, n7404_1_p8, n7404_1_p6, n7432_1_p10, n7432_1_p10, n7432_1_p4, out_4

  // Notes on the sheet:
  //   PART 4.a
endmodule
