// Logisim project part4_b.circ as structural Verilog: 2 circuits, main circuit main
module main (
  input  a,
  input  b,
  input  c,
  output F1
);

  wire decoder_1_out0, decoder_1_out6, decoder_1_out7;

  Decoder #(.select(3), .enable("false")) decoder_1 (
    .out0(decoder_1_out0), .out6(decoder_1_out6), .out7(decoder_1_out7), .sel({a, b, c}));  // open: out1, out2, out3, out4, out5
  or or_1 (F1, decoder_1_out0, decoder_1_out6, decoder_1_out7);

  // Notes on the sheet:
  //   PART 4.b
endmodule

module main2 (
  input  a,
  input  b,
  input  c,
  output out_4
);

  wire n7404_1_p2, n7404_1_p5, n7404_1_p7, n7432_1_p3, n74138_1_p7, n74138_1_p10, n74138_1_p11;

  // _74138 74138_1: pin names not known; wires that end beside it: c, b, a, 1'b0, 1'b0, 1'b1, n74138_1_p7, 1'b0, 1'b1, n74138_1_p10, n74138_1_p11
  // _7404 7404_1: pin names not known; wires that end beside it: n74138_1_p7, n7404_1_p2, 1'b1, n74138_1_p10, n7404_1_p5, n74138_1_p11, n7404_1_p7
  // _7432 7432_1: pin names not known; wires that end beside it: 1'b0, n7404_1_p2, n7432_1_p3, out_4, 1'b0, 1'b1, n7404_1_p7, n7404_1_p5, n7432_1_p3

  // Notes on the sheet:
  //   PART 4.b
endmodule
