// Logisim project part1.circ as structural Verilog: 1 circuit, main circuit main
module main (
  input  a,
  input  b
);

  wire n7408_1_p3, n7486_1_p3;

  // _7486 7486_1: pin names not known; wires that end beside it: a, b, n7486_1_p3, 1'b0, 1'b1, a, b
  // _7408 7408_1: pin names not known; wires that end beside it: a, b, n7408_1_p3, 1'b0, 1'b1
  LED Sum (.in(n7486_1_p3));
  LED Carry (.in(n7408_1_p3));

  // Notes on the sheet:
  //   GND
  //   5V
  //   PART 1
endmodule
