// Logisim project part2.circ as structural Verilog: 1 circuit, main circuit main
module main (
  input  a,
  input  b,
  input  Cin
);

  wire n7408_1_p3, n7408_1_p6, n7408_1_p11, n7432_1_p3, n7432_1_p6, n7486_1_p3, n7486_1_p6;

  // _7486 7486_1: pin names not known; wires that end beside it: a, b, n7486_1_p3, n7486_1_p3, Cin, n7486_1_p6, 1'b0, 1'b1
  // _7408 7408_1: pin names not known; wires that end beside it: a, b, n7408_1_p3, a, Cin, n7408_1_p6, 1'b0, 1'b1, b, Cin, n7408_1_p11
  // _7432 7432_1: pin names not known; wires that end beside it: n7408_1_p3, n7408_1_p6, n7432_1_p3, n7432_1_p3, n7408_1_p11, n7432_1_p6, 1'b0, 1'b1
  LED Sum (.in(n7486_1_p6));
  LED Carry (.in(n7432_1_p6));

  // Notes on the sheet:
  //   GND
  //   5V
  //   PART 2
endmodule
