// Logisim project part4.circ as structural Verilog: 1 circuit, main circuit main
module main (
  input  B0,
  input  B1,
  input  B2,
  input  B3,
  input  S0,
  input  S1,
  input  S2,
  input  S3,
  input  M,
  input  Cn,
  input  Clear
);

  wire dip_74181_1_p9, n74174_1_p1, n74174_1_p2, n74174_1_p11, n74174_1_p15;
  wire [3:0] dip_74181_1_p2, not_1_out;

  // DIP_74181 dip_74181_1: pin names not known; wires that end beside it: B0, dip_74181_1_p2[0], S3, S2, S1, S0, Cn, M, dip_74181_1_p9, dip_74181_1_p2[1], B1, dip_74181_1_p2[2], B2, dip_74181_1_p2[3], B3
  // _74174 74174_1: pin names not known; wires that end beside it: n74174_1_p1, n74174_1_p2, Clear, dip_74181_1_p2[0], dip_74181_1_p9, n74174_1_p1, dip_74181_1_p2[1], n74174_1_p2, dip_74181_1_p2[2], 1'b0, n74174_1_p11, 1'b1, n74174_1_p11, dip_74181_1_p2[3], n74174_1_p15
  assign not_1_out = ~dip_74181_1_p2;  // NOT_Gate not_1, 4 bits wide
  Hex_Digit_Display hex_digit_display_1 (.value(not_1_out));  // open: dp
  Clock clock_1 (.out(n74174_1_p15));
endmodule
