// Logisim project part2.circ as structural Verilog: 1 circuit, main circuit main
module main (
  input  a,
  input  b,
  output z1,
  output z2
);

  wire and_1_out, or_2_out;

  and and_1 (and_1_out, a, b);
  or or_1 (z1, and_1_out, a);
  or or_2 (or_2_out, a, b);
  and and_2 (z2, or_2_out, a);

  // Notes on the sheet:
  //   PART 2
  //   a
  //   b
endmodule
