// Logisim project part2_IC.circ as structural Verilog: 1 circuit, main circuit main
module main (
  input  a,
  input  b,
  output out_3,
  output out_4
);

  wire n7408_1_p3, n7432_1_p3;

  // _7408 7408_1: pin names not known; wires that end beside it: a, b, n7408_1_p3
  // _7432 7432_1: pin names not known; wires that end beside it: a, b, n7432_1_p3
  // _7432 7432_2: pin names not known; wires that end beside it: n7408_1_p3, a, out_3
  // _7408 7408_2: pin names not known; wires that end beside it: a, b, n7432_1_p3, a, out_4

  // Notes on the sheet:
  //   PART 2
endmodule
