// Logisim project part3_IC.circ as structural Verilog: 1 circuit, main circuit main
module main (
  input  a,
  input  b,
  input  c,
  output out_4
);

  wire n7404_1_p2, n7404_2_p3, n7404_3_p6, n7432_1_p2, n7432_2_p2;

  // _7404 7404_1: pin names not known; wires that end beside it: a, n7404_1_p2
  // _7432 7432_1: pin names not known; wires that end beside it: n7404_1_p2, n7432_1_p2
  // _7404 7404_2: pin names not known; wires that end beside it: b, n7432_1_p2, n7404_2_p3
  // _7432 7432_2: pin names not known; wires that end beside it: a, n7432_2_p2
  // _7404 7404_3: pin names not known; wires that end beside it: a, b, c, c, n7432_2_p2, n7404_3_p6
  // _7408 7408_1: pin names not known; wires that end beside it: n7404_2_p3, n7404_3_p6, out_4

  // Notes on the sheet:
  //   PART 3
endmodule
